# Fritzing sketch gps schematic (saved by Fritzing 0.8.7b)
breadboards: 1

parts:
  Part1 = Arduino Micro (Rev3)
  GPS1 = Adafruit Ultimate GPS Breakout
  IMU1 = Adafruit 10-DOF IMU Breakout
  microSD1 = MicroSD Breakout
  D1 = Diode [package=diode-1n4001]

nets:
  N1: Part1.MOSI, microSD1.DI
  N2: Part1.D2/SDA, IMU1.SDA
  N3: Part1.D3/SCL, IMU1.SCL
  N4: Part1.D7, GPS1.RX
  N5: Part1.D8_PWM/A8, GPS1.TX
  N6: Part1.D10_PWM/A10, microSD1.CS
  N7: Part1.SCK, microSD1.CLK
  N8: Part1.MISO, microSD1.DO
  N9: Part1.VIN, D1.A
  GND: Part1.GND, GPS1.GND, IMU1.3Vo, IMU1.GND, microSD1.GND
  5V: Part1.5V, GPS1.VIN, IMU1.VIN, microSD1.3v, microSD1.5V

custom parts:
  MicroSD Breakout: 5V-ready microSD Breakout with Level Shifter
